# Fritzing sketch Controller-Schematic-Rev_E (saved by Fritzing 0.9.10b)
breadboards: 3

parts:
  Part3 = Arduino Nano 33 IOT
  LED1 = LED - 5mm [color="Red (633nm)" current=0.030 package="5 mm [THT]"]
  LED2 = LED - 5mm [color="Red (633nm)" current=0.030 package="5 mm [THT]"]
  LED3 = LED - 5mm [color="Red (633nm)" current=0.030 package="5 mm [THT]"]
  LED4 = LED - 5mm [color="Red (633nm)" current=0.030 package="5 mm [THT]"]
  LED5 = LED - 5mm [color="Red (633nm)" current=0.030 package="5 mm [THT]"]
  LED6 = LED - 5mm [color="Red (633nm)" current=0.030 package="5 mm [THT]"]
  LED7 = LED - 5mm [color="Red (633nm)" current=0.030 package="5 mm [THT]"]
  LED8 = LED - 5mm [color="Red (633nm)" current=30mA package="5 mm [THT]"]
  R25 = Resistor [tolerance=±5% power=0.25 resistance=470 package=THT]
  R26 = Resistor [tolerance=±5% power=0.25 resistance=470 package=THT]
  R28 = Resistor [tolerance=±5% power=0.25 resistance=470 package=THT]
  R29 = Resistor [tolerance=±5% power=0.25 resistance=470 package=THT]
  R31 = Resistor [tolerance=±5% power=0.25 resistance=470 package=THT]
  R32 = Resistor [tolerance=±5% power=0.25 resistance=470 package=THT]
  LM1084-3_3V1 = Voltage Regulator - 3.3V [part_number=LM1084IT-3.3/NOPB package="TO220 [THT]"]
  C2 = Tantalum Capacitor [capacitance=10µF voltage=10V package="200 mil [THT, tantalum]"]
  C1 = Electrolytic Capacitor [capacitance=10µF voltage=16V part_number=ECA-1CM100I package="100 mil [THT, electrolytic]"]
  OX = DB9 Connector [package=db9]
  FUEL = DB9 Connector [package=db9]
  R39 = Resistor [tolerance=±5% power=0.25 resistance=470 package=THT]
  R40 = Resistor [tolerance=±5% power=0.25 resistance=470 package=THT]
  FUEL_2 = IC, DIP package, 8 pins [chip_label=LTC1690]
  OX_2 = IC, DIP package, 8 pins [chip_label=LTC1690]
  EXT = IC, DIP package, 8 pins [chip_label=LTC1690]
  SN74AXC = SSOP24 [chip_label=SN74AXC part_number=SN74AXC4T774-Q1 package=SSOP]
  74HCT595 = SO16 [chip_label=74HCT595 package=SO]
  ISO7740 = SO16 [chip_label=ISO7740 package=SO]
  ISO7741 = SO16 [chip_label=ISO7740 package=SO]
  C3 = Electrolytic Capacitor [capacitance=1µF voltage=5V package="100 mil [THT, electrolytic]"]
  C4 = Electrolytic Capacitor [capacitance=1µF voltage=5V package="100 mil [THT, electrolytic]"]
  C5 = Electrolytic Capacitor [capacitance=1µF voltage=5V package="100 mil [THT, electrolytic]"]
  C6 = Electrolytic Capacitor [capacitance=1µF voltage=5V package="100 mil [THT, electrolytic]"]
  C7 = Electrolytic Capacitor [capacitance=1µF voltage=5V package="100 mil [THT, electrolytic]"]
  C8 = Electrolytic Capacitor [capacitance=1µF voltage=5V package="100 mil [THT, electrolytic]"]
  C9 = Electrolytic Capacitor [capacitance=1µF voltage=5V package="100 mil [THT, electrolytic]"]
  C10 = Electrolytic Capacitor [capacitance=1µF voltage=5V package="100 mil [THT, electrolytic]"]
  C19 = Electrolytic Capacitor [capacitance=1µF voltage=5V package="100 mil [THT, electrolytic]"]
  C20 = Electrolytic Capacitor [capacitance=1µF voltage=5V package="100 mil [THT, electrolytic]"]
  C23 = Electrolytic Capacitor [capacitance=1µF voltage=5V package="100 mil [THT, electrolytic]"]
  C24 = Electrolytic Capacitor [capacitance=1µF voltage=5V package="100 mil [THT, electrolytic]"]
  C17 = Electrolytic Capacitor [capacitance=1µF voltage=5V package="100 mil [THT, electrolytic]"]
  C18 = Electrolytic Capacitor [capacitance=1µF voltage=5V package="100 mil [THT, electrolytic]"]
  C21 = Electrolytic Capacitor [capacitance=1µF voltage=5V package="100 mil [THT, electrolytic]"]
  C22 = Electrolytic Capacitor [capacitance=1µF voltage=5V package="100 mil [THT, electrolytic]"]
  C11 = Electrolytic Capacitor [capacitance=1µF voltage=5V package="100 mil [THT, electrolytic]"]
  C12 = Electrolytic Capacitor [capacitance=1µF voltage=5V package="100 mil [THT, electrolytic]"]
  C13 = Electrolytic Capacitor [capacitance=1µF voltage=5V package="100 mil [THT, electrolytic]"]
  C14 = Electrolytic Capacitor [capacitance=1µF voltage=5V package="100 mil [THT, electrolytic]"]
  C15 = Electrolytic Capacitor [capacitance=1µF voltage=5V package="100 mil [THT, electrolytic]"]
  C16 = Electrolytic Capacitor [capacitance=1µF voltage=5V package="100 mil [THT, electrolytic]"]
  SER_EN = single row smd female pin header, 2 pins [form="♀ (female)"]
  EXT_2 = DB9 Connector [package=db9]

nets:
  N1: Part3.RX, EXT.pin3
  N2: Part3.TX, SN74AXC.5
  N3: Part3.RESET, Part3.A7, SN74AXC.6
  GND: Part3.GND, Part3.D13~, R25.Pin_1, R26.Pin_1, R28.Pin_1, R29.Pin_1, R31.Pin_1, R32.Pin_1, LM1084-3_3V1.GND, C2.-, C1.-, R39.Pin_1, R40.Pin_1, FUEL_2.pin3, FUEL_2.pin4, OX_2.pin4, EXT.pin4, SN74AXC.2, SN74AXC.11, SN74AXC.12, SN74AXC.13, SN74AXC.22, 74HCT595.11, 74HCT595.13, C3.-, C4.-, C5.-, C6.-, C7.-, C8.-, C9.-, C10.-, C11.-, C12.-, C13.-, C14.-, C15.-, C16.-, SER_EN.pin2, EXT_2.5
  N4: Part3.D2, SN74AXC.8
  N5: Part3.D3~, SER_EN.pin1
  N6: Part3.D4, SN74AXC.4
  N7: Part3.D5~, OX_2.pin3
  N8: Part3.D8, 74HCT595.12
  N9: Part3.D9~, ISO7741.4
  N10: Part3.D10~, ISO7740.4
  N11: Part3.D11/MOSI, Part3.+5V, 74HCT595.14
  N12: Part3.D12~/MISO, SN74AXC.3
  N13: Part3.VIN, LM1084-3_3V1.output_voltage, C2.+, SN74AXC.1, ISO7740.1, ISO7741.1, C3.+, C4.+, C5.+, C6.+, C17.+, C18.+, C21.+, C22.+
  N14: Part3.A6, SN74AXC.7
  N15: Part3.A3, ISO7740.3
  N16: Part3.A2, ISO7741.3
  N17: Part3.A1, ISO7740.5
  N18: Part3.A0, ISO7741.5
  N19: LED1.cathode, R32.Pin_0
  N20: LED1.anode, 74HCT595.7
  N21: LED2.cathode, R31.Pin_0
  N22: LED2.anode, 74HCT595.6
  N23: LED3.cathode, R40.Pin_0
  N24: LED3.anode, 74HCT595.5
  N25: LED4.cathode, R29.Pin_0
  N26: LED4.anode, 74HCT595.4
  N27: LED5.cathode, R28.Pin_0
  N28: LED5.anode, 74HCT595.3
  N29: LED6.cathode, R39.Pin_0
  N30: LED6.anode, 74HCT595.2
  N31: LED7.cathode, R26.Pin_0
  N32: LED7.anode, 74HCT595.1
  N33: LED8.cathode, R25.Pin_0
  N34: LED8.anode, 74HCT595.15
  N35: LM1084-3_3V1.input_voltage, C1.+, FUEL_2.pin1, OX_2.pin1, EXT.pin1, SN74AXC.23, SN74AXC.24, 74HCT595.9, 74HCT595.10, 74HCT595.16, C7.+, C8.+, C9.+, C10.+, C11.+, C12.+, C13.+, C14.+, C15.+, C16.+, EXT_2.6
  N36: OX.1, OX_2.pin8
  N37: OX.2, OX_2.pin7
  N38: OX.3, OX_2.pin6
  N39: OX.4, OX_2.pin5
  N40: OX.5, ISO7741.10, ISO7741.16, C23.+, C24.+
  N41: OX.6, ISO7741.9, ISO7741.15, C23.-, C24.-
  N42: OX.7, ISO7741.14
  N43: OX.8, ISO7741.13
  N44: OX.9, ISO7741.12
  N45: FUEL.1, FUEL_2.pin8
  N46: FUEL.2, FUEL_2.pin7
  N47: FUEL.3, FUEL_2.pin6
  N48: FUEL.4, FUEL_2.pin5
  N49: FUEL.5, ISO7740.10, ISO7740.16, C19.+, C20.+
  N50: FUEL.6, ISO7740.9, ISO7740.15, C19.-, C20.-
  N51: FUEL.7, ISO7740.14
  N52: FUEL.8, ISO7740.13
  N53: FUEL.9, ISO7740.12
  N54: FUEL_2.pin2, SN74AXC.21
  N55: OX_2.pin2, SN74AXC.20
  N56: EXT.pin2, SN74AXC.19
  N57: EXT.pin5, EXT_2.4
  N58: EXT.pin6, EXT_2.3
  N59: EXT.pin7, EXT_2.2
  N60: SN74AXC.16, EXT_2.7
  N61: SN74AXC.17, EXT_2.8
  N62: SN74AXC.18, EXT_2.9
  N63: 74HCT595.8, ISO7740.2, ISO7740.8, ISO7741.2, ISO7741.8, C17.-, C18.-, C21.-, C22.-

custom parts:
  Arduino Nano 33 IOT: The Arduino Nano 33 IoT is the easiest and cheapest point of entry to enhance existing devices (and creating new ones) to be part of the IoT and designing pico-network applications. Whether you are looking at building a sensor network connected to your office or home router, or if you want to create a BLE device sending data to a cellphone, the Nano 33 IoT is your one-stop-solution for many of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
