# Fritzing sketch Controller-Schematic (saved by Fritzing 0.9.10b)
breadboards: 1

parts:
  U1 = MAX485 [package=dil08]
  Part1 = Arduino Nano 33 IOT
  U2 = MAX485 [package=dil08]
  VGA_FEMALE4 = DB15 VGA Connector [package=db15]
  VGA_FEMALE5 = DB15 VGA Connector [package=db15]
  U3 = MAX485 [package=dil08]
  U4 = MAX485 [package=dil08]
  R1 = Resistor [tolerance=±5% power=0.25 resistance=220 package=THT]
  R2 = Resistor [tolerance=±5% power=0.25 resistance=220 package=THT]
  R3 = Resistor [tolerance=±5% power=0.25 resistance=220 package=THT]
  R4 = Resistor [tolerance=±5% power=0.25 resistance=220 package=THT]
  R5 = Resistor [tolerance=±5% power=0.25 resistance=220 package=THT]
  R6 = Resistor [tolerance=±5% power=0.25 resistance=220 package=THT]
  R7 = Resistor [tolerance=±5% power=0.25 resistance=220 package=THT]
  R8 = Resistor [tolerance=±5% power=0.25 resistance=220 package=THT]

nets:
  N1: U1.RO, Part1.RX
  N2: U1.RE, R3.Pin_0
  GND: U1.GND, U2.GND, VGA_FEMALE4.GND, VGA_FEMALE5.GND, U3.GND, U4.GND, R3.Pin_1, R4.Pin_0
  N3: U1.A, VGA_FEMALE4.CLK-
  N4: U1.B, VGA_FEMALE4.CLK+
  VCC: U1.VCC, U2.VCC, VGA_FEMALE4.5V, VGA_FEMALE5.5V, U3.VCC, U4.VCC, R1.Pin_1, R2.Pin_1, R5.Pin_1, R6.Pin_0
  N5: Part1.TX, U2.DI
  N6: Part1.RESET, Part1.A7, VGA_FEMALE5.ADJ-R
  N7: Part1.GND, Part1.D13~, VGA_FEMALE4.ADJ-L
  N8: Part1.D2, VGA_FEMALE4.ADJ-R
  N9: Part1.D3~, VGA_FEMALE5.ADJ-L
  N10: Part1.D4, VGA_FEMALE5.DIR
  N11: Part1.D5~, VGA_FEMALE4.DIR
  N12: Part1.D6~, R7.Pin_1
  N13: Part1.D7, R8.Pin_1
  N14: Part1.D8, VGA_FEMALE5.CTRL
  N15: Part1.D10~, VGA_FEMALE4.CTRL
  N16: Part1.D11/MOSI, Part1.+5V, U3.DI
  N17: Part1.D12~/MISO, U4.RO
  N18: Part1.A6, VGA_FEMALE4.H3
  N19: Part1.A5, VGA_FEMALE4.H2
  N20: Part1.A4, VGA_FEMALE4.H1
  N21: Part1.A3, VGA_FEMALE5.H1
  N22: Part1.A2, VGA_FEMALE5.H2
  N23: Part1.A1, VGA_FEMALE5.H3
  N24: U2.DE, R5.Pin_0
  N25: U2.A, VGA_FEMALE4.DATA-
  N26: U2.B, VGA_FEMALE4.DATA+
  N27: VGA_FEMALE4.STOP, R7.Pin_0
  N28: VGA_FEMALE4.ADJ+, R1.Pin_0
  N29: VGA_FEMALE5.CLK+, U4.A
  N30: VGA_FEMALE5.CLK-, U4.B
  N31: VGA_FEMALE5.DATA+, U3.A
  N32: VGA_FEMALE5.DATA-, U3.B
  N33: VGA_FEMALE5.STOP, R8.Pin_0
  N34: VGA_FEMALE5.ADJ+, R2.Pin_0
  N35: U3.DE, R6.Pin_1
  N36: U4.RE, R4.Pin_1

custom parts:
  Arduino Nano 33 IOT: The Arduino Nano 33 IoT is the easiest and cheapest point of entry to enhance existing devices (and creating new ones) to be part of the IoT and designing pico-network applications. Whether you are looking at building a sensor network connected to your office or home router, or if you want to create a BLE device sending data to a cellphone, the Nano 33 IoT is your one-stop-solution for many of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
